// Logisim project ITP_Computer.circ as structural Verilog: 10 circuits, main circuit main
module main (
  input  in_1,
  input  READ_RAM,
  input  KEYBOARD_INPUT
);

  wire alu_1_borrow_out, alu_1_carry_out, alu_1_equals, alu_1_greater, alu_1_less, alu_1_zero_flag,
       clock_1_out, clock_cst_1_clock_output;
  wire [6:0] keyboard_1_data;
  wire [7:0] frame_buffer_1_out_9, frame_buffer_1_out_10, frame_buffer_1_out_11, frame_buffer_1_out_12,
       frame_buffer_1_out_13, frame_buffer_1_out_14, frame_buffer_1_out_15, frame_buffer_1_out_16;
  wire [15:0] accumulator_1_always_out, b_register_1_always_out, memory_address_register_1_always_out,
       memory_address_register_1_data_out, program_counter_1_always_out, ram_1_dout;

  MEMORY_ADDRESS_REGISTEr memory_address_register_1 (
    .DATA_IN(memory_address_register_1_data_out), .CLOCK(clock_cst_1_clock_output),
    .ALWAYS_OUT(memory_address_register_1_always_out), .DATA_OUT(memory_address_register_1_data_out));  // open: ADDRESS_WRITE, RESET, ADDRESS_READ
  RAM #(.addrWidth(16), .dataWidth(16), .enables("line")) ram_1 (
    .addr(memory_address_register_1_always_out), .clk(clock_cst_1_clock_output),
    .din(memory_address_register_1_data_out), .dout(ram_1_dout));  // open: we
  LED led_1 (.in(memory_address_register_1_data_out[15]));
  assign memory_address_register_1_data_out = READ_RAM ? ram_1_dout : 16'bz;  // Controlled_Buffer controlled_buffer_1
  LED led_2 (.in(memory_address_register_1_data_out[14]));
  LED led_3 (.in(memory_address_register_1_data_out[13]));
  LED led_4 (.in(memory_address_register_1_data_out[12]));
  LED led_5 (.in(memory_address_register_1_data_out[11]));
  LED led_6 (.in(memory_address_register_1_data_out[10]));
  LED led_7 (.in(memory_address_register_1_data_out[9]));
  LED led_8 (.in(memory_address_register_1_data_out[8]));
  LED led_9 (.in(memory_address_register_1_data_out[7]));
  LED led_10 (.in(memory_address_register_1_data_out[6]));
  LED led_11 (.in(memory_address_register_1_data_out[5]));
  LED led_12 (.in(memory_address_register_1_data_out[4]));
  LED led_13 (.in(memory_address_register_1_data_out[3]));
  LED led_14 (.in(memory_address_register_1_data_out[2]));
  LED led_15 (.in(memory_address_register_1_data_out[1]));
  LED led_16 (.in(memory_address_register_1_data_out[0]));
  Clock clock_1 (.out(clock_1_out));
  CLOCK_CST clock_cst_1 (
    .CLOCK_IN(clock_1_out), .CLOCK_ENABLE(in_1), .CLOCK_OUTPUT(clock_cst_1_clock_output));  // open: MANUAL_TICK, STOP
  LED led_17 (.in(program_counter_1_always_out[15]));
  LED led_18 (.in(program_counter_1_always_out[14]));
  LED led_19 (.in(program_counter_1_always_out[13]));
  LED led_20 (.in(program_counter_1_always_out[12]));
  LED led_21 (.in(program_counter_1_always_out[11]));
  LED led_22 (.in(program_counter_1_always_out[10]));
  LED led_23 (.in(program_counter_1_always_out[9]));
  LED led_24 (.in(program_counter_1_always_out[8]));
  ACCUMULATOR accumulator_1 (
    .DATA_IN(memory_address_register_1_data_out), .CLOCK(clock_cst_1_clock_output),
    .ALWAYS_OUT(accumulator_1_always_out), .DATA_OUT(memory_address_register_1_data_out));  // open: A_WRITE, A_READ, RESET
  B_REGISTER b_register_1 (
    .CLOCK(clock_cst_1_clock_output), .DATA_INPUT(memory_address_register_1_data_out),
    .ALWAYS_OUT(b_register_1_always_out), .DATA_OUTPUT(memory_address_register_1_data_out));  // open: B_WRITE, B_READ, RESET
  LED led_25 (.in(program_counter_1_always_out[7]));
  LED led_26 (.in(program_counter_1_always_out[6]));
  LED led_27 (.in(program_counter_1_always_out[5]));
  LED led_28 (.in(program_counter_1_always_out[4]));
  PROGRAM_COUNTER program_counter_1 (
    .CLOCK(clock_cst_1_clock_output), .ADDRESS_IN(memory_address_register_1_data_out),
    .ALWAYS_OUT(program_counter_1_always_out), .ADDRESS_OUT(memory_address_register_1_data_out));  // open: RESET, JUMP, COUNTER_ENABLE, COUNTER_OUT
  ALU alu_1 (
    .A_IN(accumulator_1_always_out), .B_IN(b_register_1_always_out), .CARRY_OUT(alu_1_carry_out),
    .BORROW_OUT(alu_1_borrow_out), .DATA_OUT(memory_address_register_1_data_out),
    .ZERO_FLAG(alu_1_zero_flag), .GREATER(alu_1_greater), .EQUALS(alu_1_equals), .LESS(alu_1_less));  // open: A_NOR_B, ADD, SUB, NOT_A, A_AND_B, A_OR_B, A_XOR_B, A_NAND_B, BORROW_IN, CARRY_IN
  X_Y_REGISTERS x_y_registers_1 (
    .DATA_IN(memory_address_register_1_data_out), .CLOCK(clock_cst_1_clock_output),
    .DATA_OUT(memory_address_register_1_data_out));  // open: READ_Y, WRITE_X, WRITE_Y, RESET, READ_X, ALWAYS_OUT_X, ALWAYS_OUT_Y
  LED led_29 (.in(program_counter_1_always_out[3]));
  LED led_30 (.in(program_counter_1_always_out[2]));
  LED led_31 (.in(program_counter_1_always_out[1]));
  LED led_32 (.in(program_counter_1_always_out[0]));
  FLAG_REGISTER flag_register_1 (
    .CARRY(alu_1_carry_out), .BORROW(alu_1_borrow_out), .GREATER(alu_1_greater), .EQUALS(alu_1_equals),
    .LESS(alu_1_less), .ZERO(alu_1_zero_flag), .CLOCK(clock_cst_1_clock_output));  // open: FLAGS_MATH, FLAGS_COMPARE, RESET, BORROW_FLAG, GREATER_FLAG, EQUALS_FLAG, LESS_FLAG, ZERO_FLAG, CARRY_FLAG
  DotMatrix #(.inputtype("row"), .matrixcols(8), .matrixrows(8)) dotmatrix_1 (
    .row0(frame_buffer_1_out_9), .row1(frame_buffer_1_out_10), .row2(frame_buffer_1_out_11),
    .row3(frame_buffer_1_out_12), .row4(frame_buffer_1_out_13), .row5(frame_buffer_1_out_14),
    .row6(frame_buffer_1_out_15), .row7(frame_buffer_1_out_16));
  FRAME_BUFFER frame_buffer_1 (
    .ADDRESS_SELECTION(memory_address_register_1_data_out[2:0]), .CLOCK(clock_cst_1_clock_output),
    .DATA_IN(memory_address_register_1_data_out[7:0]), .out_9(frame_buffer_1_out_9),
    .out_10(frame_buffer_1_out_10), .out_11(frame_buffer_1_out_11), .out_12(frame_buffer_1_out_12),
    .out_13(frame_buffer_1_out_13), .out_14(frame_buffer_1_out_14), .out_15(frame_buffer_1_out_15),
    .out_16(frame_buffer_1_out_16));  // open: RESET_BUFFER, UPDATE_DISPLAY, RESET_DISPLAY, BUFFER_ADDRESS_WRITE, DATA_WRITE
  TTY tty_1 (.data(memory_address_register_1_data_out[6:0]), .clk(clock_cst_1_clock_output));  // open: we, clr
  Keyboard keyboard_1 (.data(keyboard_1_data));  // open: clk, re, clr, avail
  assign memory_address_register_1_data_out[6:0] = KEYBOARD_INPUT ? keyboard_1_data : 7'bz;  // Controlled_Buffer controlled_buffer_2
  Pull_Resistor pull_resistor_1 (.node(memory_address_register_1_data_out[0]));
  Pull_Resistor pull_resistor_2 (.node(memory_address_register_1_data_out[1]));
  Pull_Resistor pull_resistor_3 (.node(memory_address_register_1_data_out[2]));
  Pull_Resistor pull_resistor_4 (.node(memory_address_register_1_data_out[3]));
  Pull_Resistor pull_resistor_5 (.node(memory_address_register_1_data_out[4]));
  Pull_Resistor pull_resistor_6 (.node(memory_address_register_1_data_out[5]));
  Pull_Resistor pull_resistor_7 (.node(memory_address_register_1_data_out[6]));
  Pull_Resistor pull_resistor_8 (.node(memory_address_register_1_data_out[7]));
  Pull_Resistor pull_resistor_9 (.node(memory_address_register_1_data_out[8]));
  Pull_Resistor pull_resistor_10 (.node(memory_address_register_1_data_out[9]));
  Pull_Resistor pull_resistor_11 (.node(memory_address_register_1_data_out[10]));
  Pull_Resistor pull_resistor_12 (.node(memory_address_register_1_data_out[11]));
  Pull_Resistor pull_resistor_13 (.node(memory_address_register_1_data_out[12]));
  Pull_Resistor pull_resistor_14 (.node(memory_address_register_1_data_out[13]));
  Pull_Resistor pull_resistor_15 (.node(memory_address_register_1_data_out[14]));
  Pull_Resistor pull_resistor_16 (.node(memory_address_register_1_data_out[15]));

  // Notes on the sheet:
  //   MAIN LINE
endmodule

module CLOCK_CST (
  input  CLOCK_IN,
  input  CLOCK_ENABLE,
  input  MANUAL_TICK,
  input  STOP,
  output CLOCK_OUTPUT
);

  wire and_1_out, and_2_out, not_1_out, not_2_out, or_1_out;

  not not_1 (not_1_out, CLOCK_ENABLE);
  and and_1 (and_1_out, CLOCK_IN, CLOCK_ENABLE);
  and and_2 (and_2_out, not_1_out, MANUAL_TICK);
  or or_1 (or_1_out, and_1_out, and_2_out);
  not not_2 (not_2_out, STOP);
  and and_3 (CLOCK_OUTPUT, or_1_out, not_2_out);
endmodule

module PROGRAM_COUNTER (
  input  RESET,
  input  JUMP,
  input  COUNTER_ENABLE,
  input  CLOCK,
  input  [15:0] ADDRESS_IN,
  input  COUNTER_OUT,
  output [15:0] ALWAYS_OUT,
  output [15:0] ADDRESS_OUT
);

  Counter #(.max('hffff), .width(16)) counter_1 (
    .clr(RESET), .load(JUMP), .up(COUNTER_ENABLE), .count(COUNTER_ENABLE), .clk(CLOCK), .D(ADDRESS_IN),
    .Q(ALWAYS_OUT));  // open: carry
  assign ADDRESS_OUT = COUNTER_OUT ? ALWAYS_OUT : 16'bz;  // Controlled_Buffer controlled_buffer_1
endmodule

module ACCUMULATOR (
  input  [15:0] DATA_IN,
  input  A_WRITE,
  input  A_READ,
  input  CLOCK,
  input  RESET,
  output [15:0] ALWAYS_OUT,
  output [15:0] DATA_OUT
);

  Register #(.width(16)) register_1 (.D(DATA_IN), .en(A_WRITE), .clk(CLOCK), .Q(ALWAYS_OUT), .clr(RESET));
  assign DATA_OUT = A_READ ? ALWAYS_OUT : 16'bz;  // Controlled_Buffer controlled_buffer_1
endmodule

module ALU (
  input  BORROW_IN,
  input  CARRY_IN,
  input  [15:0] A_IN,
  input  [15:0] B_IN,
  input  ADD,
  input  SUB,
  input  NOT_A,
  input  A_AND_B,
  input  A_OR_B,
  input  A_XOR_B,
  input  A_NAND_B,
  input  A_NOR_B,
  output CARRY_OUT,
  output BORROW_OUT,
  output GREATER,
  output EQUALS,
  output LESS,
  output [15:0] DATA_OUT,
  output ZERO_FLAG
);

  wire and_2_out, and_3_out, and_4_out, and_5_out, and_6_out, and_7_out, and_8_out, and_9_out, and_10_out,
       and_11_out, and_12_out, and_13_out, and_14_out, and_15_out, not_2_out, not_3_out, not_4_out,
       not_5_out, not_6_out, not_7_out, not_8_out, not_9_out, not_10_out, not_11_out, not_12_out, not_13_out,
       not_14_out, not_15_out, not_16_out, not_17_out;
  wire [15:0] adder_1_out, and_1_out, nand_1_out, nor_1_out, not_1_out, or_1_out, or_2_out, subtractor_1_out,
       xor_1_out;

  Adder #(.width(16)) adder_1 (.a(A_IN), .b(B_IN), .out(adder_1_out), .cin(CARRY_IN), .cout(CARRY_OUT));
  Subtractor #(.width(16)) subtractor_1 (
    .a(A_IN), .b(B_IN), .out(subtractor_1_out), .bin(BORROW_IN), .bout(BORROW_OUT));
  Comparator #(.width(16)) comparator_1 (.a(A_IN), .b(B_IN), .gt(GREATER), .eq(EQUALS), .lt(LESS));
  assign not_1_out = ~A_IN;  // NOT_Gate not_1, 16 bits wide
  assign and_1_out = A_IN & B_IN;  // AND_Gate and_1, 16 bits wide
  assign or_1_out = A_IN | B_IN;  // OR_Gate or_1, 16 bits wide
  assign xor_1_out = A_IN ^ B_IN;  // XOR_Gate xor_1, 16 bits wide
  assign nand_1_out = ~(A_IN & B_IN);  // NAND_Gate nand_1, 16 bits wide
  assign nor_1_out = ~(A_IN | B_IN);  // NOR_Gate nor_1, 16 bits wide
  assign DATA_OUT = ADD ? adder_1_out : 16'bz;  // Controlled_Buffer controlled_buffer_1
  assign DATA_OUT = SUB ? subtractor_1_out : 16'bz;  // Controlled_Buffer controlled_buffer_2
  assign DATA_OUT = NOT_A ? not_1_out : 16'bz;  // Controlled_Buffer controlled_buffer_3
  assign DATA_OUT = A_AND_B ? and_1_out : 16'bz;  // Controlled_Buffer controlled_buffer_4
  assign DATA_OUT = A_OR_B ? or_1_out : 16'bz;  // Controlled_Buffer controlled_buffer_5
  assign DATA_OUT = A_XOR_B ? xor_1_out : 16'bz;  // Controlled_Buffer controlled_buffer_6
  assign DATA_OUT = A_NAND_B ? nand_1_out : 16'bz;  // Controlled_Buffer controlled_buffer_7
  assign DATA_OUT = A_NOR_B ? nor_1_out : 16'bz;  // Controlled_Buffer controlled_buffer_8
  assign or_2_out = DATA_OUT;  // OR_Gate or_2, 16 bits wide OR_Gate
  not not_2 (not_2_out, or_2_out[0]);
  not not_3 (not_3_out, or_2_out[1]);
  not not_4 (not_4_out, or_2_out[2]);
  not not_5 (not_5_out, or_2_out[3]);
  and and_2 (and_2_out, not_2_out, not_3_out);
  and and_3 (and_3_out, and_2_out, not_4_out);
  and and_4 (and_4_out, and_3_out, not_5_out);
  and and_5 (and_5_out, and_4_out, not_6_out);
  not not_6 (not_6_out, or_2_out[4]);
  not not_7 (not_7_out, or_2_out[5]);
  not not_8 (not_8_out, or_2_out[6]);
  not not_9 (not_9_out, or_2_out[7]);
  and and_6 (and_6_out, and_5_out, not_7_out);
  and and_7 (and_7_out, and_6_out, not_8_out);
  and and_8 (and_8_out, and_7_out, not_9_out);
  and and_9 (and_9_out, and_8_out, not_10_out);
  not not_10 (not_10_out, or_2_out[8]);
  not not_11 (not_11_out, or_2_out[9]);
  not not_12 (not_12_out, or_2_out[10]);
  not not_13 (not_13_out, or_2_out[11]);
  and and_10 (and_10_out, and_9_out, not_11_out);
  and and_11 (and_11_out, and_10_out, not_12_out);
  and and_12 (and_12_out, and_11_out, not_13_out);
  and and_13 (and_13_out, and_12_out, not_14_out);
  not not_14 (not_14_out, or_2_out[12]);
  not not_15 (not_15_out, or_2_out[13]);
  not not_16 (not_16_out, or_2_out[14]);
  not not_17 (not_17_out, or_2_out[15]);
  and and_14 (and_14_out, and_13_out, not_15_out);
  and and_15 (and_15_out, and_14_out, not_16_out);
  and and_16 (ZERO_FLAG, and_15_out, not_17_out);
  Pull_Resistor pull_resistor_1 (.node(or_2_out[0]));
  Pull_Resistor pull_resistor_2 (.node(or_2_out[1]));
  Pull_Resistor pull_resistor_3 (.node(or_2_out[2]));
  Pull_Resistor pull_resistor_4 (.node(or_2_out[3]));
  Pull_Resistor pull_resistor_5 (.node(or_2_out[4]));
  Pull_Resistor pull_resistor_6 (.node(or_2_out[5]));
  Pull_Resistor pull_resistor_7 (.node(or_2_out[6]));
  Pull_Resistor pull_resistor_8 (.node(or_2_out[7]));
  Pull_Resistor pull_resistor_9 (.node(or_2_out[8]));
  Pull_Resistor pull_resistor_10 (.node(or_2_out[9]));
  Pull_Resistor pull_resistor_11 (.node(or_2_out[10]));
  Pull_Resistor pull_resistor_12 (.node(or_2_out[11]));
  Pull_Resistor pull_resistor_13 (.node(or_2_out[12]));
  Pull_Resistor pull_resistor_14 (.node(or_2_out[13]));
  Pull_Resistor pull_resistor_15 (.node(or_2_out[14]));
  Pull_Resistor pull_resistor_16 (.node(or_2_out[15]));
endmodule

module FLAG_REGISTER (
  input  CARRY,
  input  BORROW,
  input  GREATER,
  input  EQUALS,
  input  LESS,
  input  ZERO,
  input  FLAGS_MATH,
  input  FLAGS_COMPARE,
  input  CLOCK,
  input  RESET,
  output CARRY_FLAG,
  output BORROW_FLAG,
  output GREATER_FLAG,
  output EQUALS_FLAG,
  output LESS_FLAG,
  output ZERO_FLAG
);

  Register #(.width(1)) register_1 (.D(CARRY), .en(FLAGS_MATH), .clk(CLOCK), .Q(CARRY_FLAG), .clr(RESET));
  Register #(.width(1)) register_2 (.D(BORROW), .en(FLAGS_MATH), .clk(CLOCK), .Q(BORROW_FLAG), .clr(RESET));
  Register #(.width(1)) register_3 (.D(GREATER), .en(FLAGS_COMPARE), .clk(CLOCK), .Q(GREATER_FLAG), .clr(RESET));
  Register #(.width(1)) register_4 (.D(EQUALS), .en(FLAGS_COMPARE), .clk(CLOCK), .Q(EQUALS_FLAG), .clr(RESET));
  Register #(.width(1)) register_5 (.D(LESS), .en(FLAGS_COMPARE), .clk(CLOCK), .Q(LESS_FLAG), .clr(RESET));
  Register #(.width(1)) register_6 (.D(ZERO), .en(FLAGS_MATH), .clk(CLOCK), .Q(ZERO_FLAG), .clr(RESET));
endmodule

module B_REGISTER (
  input  [15:0] DATA_INPUT,
  input  B_WRITE,
  input  B_READ,
  input  CLOCK,
  input  RESET,
  output [15:0] ALWAYS_OUT,
  output [15:0] DATA_OUTPUT
);

  Register #(.width(16)) register_1 (.D(DATA_INPUT), .en(B_WRITE), .clk(CLOCK), .Q(ALWAYS_OUT), .clr(RESET));
  assign DATA_OUTPUT = B_READ ? ALWAYS_OUT : 16'bz;  // Controlled_Buffer controlled_buffer_1
endmodule

module X_Y_REGISTERS (
  input  CLOCK,
  input  [15:0] DATA_IN,
  input  WRITE_X,
  input  WRITE_Y,
  input  RESET,
  input  READ_X,
  input  READ_Y,
  output [15:0] ALWAYS_OUT_X,
  output [15:0] DATA_OUT,
  output [15:0] ALWAYS_OUT_Y
);

  Register #(.width(16)) register_1 (.D(DATA_IN), .en(WRITE_X), .clk(CLOCK), .Q(ALWAYS_OUT_X), .clr(RESET));
  Register #(.width(16)) register_2 (.D(DATA_IN), .en(WRITE_Y), .clk(CLOCK), .Q(ALWAYS_OUT_Y), .clr(RESET));
  assign DATA_OUT = READ_X ? ALWAYS_OUT_X : 16'bz;  // Controlled_Buffer controlled_buffer_1
  assign DATA_OUT = READ_Y ? ALWAYS_OUT_Y : 16'bz;  // Controlled_Buffer controlled_buffer_2
endmodule

module FRAME_BUFFER (
  input  [7:0] DATA_IN,
  input  DATA_WRITE,
  input  [2:0] ADDRESS_SELECTION,
  input  BUFFER_ADDRESS_WRITE,
  input  CLOCK,
  input  UPDATE_DISPLAY,
  input  RESET_BUFFER,
  input  RESET_DISPLAY,
  output [7:0] out_9,
  output [7:0] out_10,
  output [7:0] out_11,
  output [7:0] out_12,
  output [7:0] out_13,
  output [7:0] out_14,
  output [7:0] out_15,
  output [7:0] out_16
);

  wire demultiplexer_1_out0, demultiplexer_1_out1, demultiplexer_1_out2, demultiplexer_1_out3,
       demultiplexer_1_out4, demultiplexer_1_out5, demultiplexer_1_out6, demultiplexer_1_out7;
  wire [2:0] register_1_q;
  wire [7:0] register_2_q, register_3_q, register_4_q, register_5_q, register_6_q, register_7_q,
       register_8_q, register_9_q;

  Register #(.width(3)) register_1 (
    .D(ADDRESS_SELECTION), .en(BUFFER_ADDRESS_WRITE), .clk(CLOCK), .Q(register_1_q));  // open: clr
  Demultiplexer #(.select(3)) demultiplexer_1 (
    .out0(demultiplexer_1_out0), .out1(demultiplexer_1_out1), .out2(demultiplexer_1_out2),
    .out3(demultiplexer_1_out3), .out4(demultiplexer_1_out4), .out5(demultiplexer_1_out5),
    .out6(demultiplexer_1_out6), .out7(demultiplexer_1_out7), .in(DATA_WRITE), .sel(register_1_q));
  Register register_2 (.D(DATA_IN), .en(demultiplexer_1_out1), .clk(CLOCK), .Q(register_2_q), .clr(RESET_BUFFER));
  Register register_3 (.D(DATA_IN), .en(demultiplexer_1_out3), .clk(CLOCK), .Q(register_3_q), .clr(RESET_BUFFER));
  Register register_4 (.D(DATA_IN), .en(demultiplexer_1_out5), .clk(CLOCK), .Q(register_4_q), .clr(RESET_BUFFER));
  Register register_5 (.D(DATA_IN), .en(demultiplexer_1_out7), .clk(CLOCK), .Q(register_5_q), .clr(RESET_BUFFER));
  Register register_6 (.D(DATA_IN), .en(demultiplexer_1_out0), .clk(CLOCK), .Q(register_6_q), .clr(RESET_BUFFER));
  Register register_7 (.D(DATA_IN), .en(demultiplexer_1_out2), .clk(CLOCK), .Q(register_7_q), .clr(RESET_BUFFER));
  Register register_8 (.D(DATA_IN), .en(demultiplexer_1_out4), .clk(CLOCK), .Q(register_8_q), .clr(RESET_BUFFER));
  Register register_9 (.D(DATA_IN), .en(demultiplexer_1_out6), .clk(CLOCK), .Q(register_9_q), .clr(RESET_BUFFER));
  Register register_10 (.D(register_2_q), .en(UPDATE_DISPLAY), .clk(CLOCK), .Q(out_10), .clr(RESET_DISPLAY));
  Register register_11 (.D(register_3_q), .en(UPDATE_DISPLAY), .clk(CLOCK), .Q(out_12), .clr(RESET_DISPLAY));
  Register register_12 (.D(register_4_q), .en(UPDATE_DISPLAY), .clk(CLOCK), .Q(out_14), .clr(RESET_DISPLAY));
  Register register_13 (.D(register_5_q), .en(UPDATE_DISPLAY), .clk(CLOCK), .Q(out_16), .clr(RESET_DISPLAY));
  Register register_14 (.D(register_6_q), .en(UPDATE_DISPLAY), .clk(CLOCK), .Q(out_9), .clr(RESET_DISPLAY));
  Register register_15 (.D(register_7_q), .en(UPDATE_DISPLAY), .clk(CLOCK), .Q(out_11), .clr(RESET_DISPLAY));
  Register register_16 (.D(register_8_q), .en(UPDATE_DISPLAY), .clk(CLOCK), .Q(out_13), .clr(RESET_DISPLAY));
  Register register_17 (.D(register_9_q), .en(UPDATE_DISPLAY), .clk(CLOCK), .Q(out_15), .clr(RESET_DISPLAY));

  // Notes on the sheet:
  //   ROZŠÍŘIT POKUD POTŘEBA VÍCE MOŽNOSTÍ DISPLAYNOUT
endmodule

module MEMORY_ADDRESS_REGISTEr (
  input  [15:0] DATA_IN,
  input  ADDRESS_WRITE,
  input  CLOCK,
  input  RESET,
  input  ADDRESS_READ,
  output [15:0] ALWAYS_OUT,
  output [15:0] DATA_OUT
);

  Register #(.width(16)) register_1 (.D(DATA_IN), .en(ADDRESS_WRITE), .clk(CLOCK), .Q(ALWAYS_OUT), .clr(RESET));
  assign DATA_OUT = ADDRESS_READ ? ALWAYS_OUT : 16'bz;  // Controlled_Buffer controlled_buffer_1
endmodule
